# Fritzing sketch Wiring Diagram (saved by Fritzing 1.0.4)
breadboards: 1

parts:
  Hot_Tub_Thermistor = Temperature Sensor (Thermistor) [thermistor_type=NTC package=THT]
  R2 = Resistor [tolerance=±0.05% resistance=15k power=0.25W package="0805 [SMD]"]
  Part1 = Adafruit Metro ESP32-S3 [part_number="Adafruit #5500"]
  1-Wire_Temp_Probe = DS18B20 1-Wire Temperature Sensor Probe Cable
  Pullup_Resistor = Resistor [tolerance=±5% power=0.25W resistance=4.7k package=THT]
  Ceramic_Capacitor = Ceramic Capacitor [capacitance=0.1µF voltage=35V package="0603 [SMD, multilayer]"]
  RE1 = KY-040 Rotary encoder [package="Breakout board"]

nets:
  GND: Hot_Tub_Thermistor.pin_0, Part1.GND, 1-Wire_Temp_Probe.GND, Ceramic_Capacitor.1, RE1.GND
  N1: Hot_Tub_Thermistor.pin_1, R2.Pin_1, Part1.D4, Ceramic_Capacitor.0
  N2: R2.Pin_0, Part1.D3
  N3: Part1.AD0, RE1.CLK
  N4: Part1.AD1, RE1.DT
  N5: Part1.AD2, RE1.SW
  N6: Part1.D2, 1-Wire_Temp_Probe.DQ, Pullup_Resistor.Pin_0
  3.3V: Part1.3.3V, 1-Wire_Temp_Probe.VDD, Pullup_Resistor.Pin_1
  N7: Part1.VHIGH, RE1.Vcc

notes:
  GND Blue or Black
  Data Yellow or White
  VDD Red (3-5V)
  • Thremistor should pull to GND as shown in this diagram. Helps protect it.
  • 0.1µF Ceramic Bypass Cap should go as close as possible to ADC pin.
  • Analog Input must be on ADC1 pins if Wi-Fi is used.

custom parts:
  Adafruit Metro ESP32-S3: What's Metro-shaped and has an ESP32-S3 WiFi module? What has a STEMMA QT connector for I2C devices and a Lipoly charger circuit? What has your favorite Espressif WiFi microcontroller and lots of memory for your next IoT project? That's right - it's the new Adafruit Metro ESP32-S3! With native USB and a load of PSRAM, this board is perfect for use with CircuitPython or Arduino to add low-cost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
  KY-040 Rotary encoder: KY-040 Rotary Encoder with switch on breakout borad from AZ Delivery
